# Fritzing sketch potentiometer-control-light-blink-value (saved by Fritzing 0.9.2b)
breadboards: 1

parts:
  Part1 = Arduino Uno (Rev3) - ICSP
  R1 = Trimmer Potentiometer [maximum_resistance=10kΩ package=THT]
  LED1 = LED - 3mm [color="Yellow (585nm)" package="3 mm [THT]"]
  R2 = Resistor [tolerance=±5% resistance=220 package="0402 [SMD]"]

nets:
  N1: Part1.A0, R1.wiper
  N2: Part1.D2, R2.Pin_0
  N3: Part1.5V, R1.leg1
  N4: Part1.GND, R1.leg2, LED1.cathode
  N5: LED1.anode, R2.Pin_1
